# Fritzing sketch AutonmousMobileRobot1 (saved by Fritzing 0.9.4)
breadboards: 1

parts:
  M1_LeftMotor = DC Motor
  U2 = L298_BRIDGE_DRIVER [package=powerso20]
  M2_RightMotor = DC Motor
  ArduinoMega2560 = Arduino Mega 2560 (Rev3)
  DC_StepDown_5V_5A_BuckConverter = RioRand LM2596
  11_1V_2200_mAh_LiPo_Battery = Battery Holders [package=lipo-1100mAh]
  MG90_GripperControl = Basic Servo
  MG90_WristRotation = Basic Servo
  MG995_ElbowRotation = Basic Servo
  MG995_ShoulderRotation = Basic Servo
  MG90_WristLift = Basic Servo
  HC-05_Bluetooth_Module = Bluetooth HC-05 Macho
  R1 = Resistor [tolerance=±5% resistance=1k package=THT]
  R2 = Resistor [tolerance=±5% resistance=2.2k package=THT]
  LeftMotor_Encoder = DIP - 4 pins [chip_label=HallEffectMotorEncoder package="DIP (Dual Inline) [THT]"]
  RightMotor_Encoder = DIP - 4 pins [chip_label=HallEffectMotorEncoder package="DIP (Dual Inline) [THT]"]

nets:
  N1: M1_LeftMotor.pin_1, U2.OUT1
  N2: M1_LeftMotor.pin_2, U2.OUT2
  N3: U2.VS, DC_StepDown_5V_5A_BuckConverter.Pin_1, 11_1V_2200_mAh_LiPo_Battery.+
  N4: U2.IN1, ArduinoMega2560.D12_PWM
  N5: U2.ENA, ArduinoMega2560.D13_PWM
  N6: U2.IN2, ArduinoMega2560.D11_PWM
  GND: U2.GND, ArduinoMega2560.GND, HC-05_Bluetooth_Module.GND, R2.Pin_1, LeftMotor_Encoder.GND, RightMotor_Encoder.GND
  VCC: U2.VSS, ArduinoMega2560.IOREF, HC-05_Bluetooth_Module.VCC, LeftMotor_Encoder.VCC, RightMotor_Encoder.VCC
  N7: U2.IN3, ArduinoMega2560.D8_PWM
  N8: U2.ENB, ArduinoMega2560.D10_PWM
  N9: U2.IN4, ArduinoMega2560.D9_PWM
  N10: U2.OUT3, M2_RightMotor.pin_1
  N11: U2.OUT4, M2_RightMotor.pin_2
  N12: ArduinoMega2560.D19/RX1, RightMotor_Encoder.SEN_A
  N13: ArduinoMega2560.D18/TX1, LeftMotor_Encoder.SEN_A
  N14: ArduinoMega2560.D15/RX3, HC-05_Bluetooth_Module.RXD
  N15: ArduinoMega2560.D14/TX3, R1.Pin_0
  N16: ArduinoMega2560.D2_PWM, MG90_GripperControl.pulse
  N17: ArduinoMega2560.D4_PWM, MG90_WristLift.pulse
  N18: ArduinoMega2560.D5_PWM, MG90_WristRotation.pulse
  N19: ArduinoMega2560.D6_PWM, MG995_ElbowRotation.pulse
  N20: ArduinoMega2560.D7_PWM, MG995_ShoulderRotation.pulse
  N21: DC_StepDown_5V_5A_BuckConverter.Pin_2, 11_1V_2200_mAh_LiPo_Battery.-
  VCC_2: DC_StepDown_5V_5A_BuckConverter.Pin_3, MG90_GripperControl.vcc, MG90_WristRotation.vcc, MG995_ElbowRotation.vcc, MG995_ShoulderRotation.vcc, MG90_WristLift.vcc
  GND_2: DC_StepDown_5V_5A_BuckConverter.Pin_4, MG90_GripperControl.gnd, MG90_WristRotation.gnd, MG995_ElbowRotation.gnd, MG995_ShoulderRotation.gnd, MG90_WristLift.gnd
  N22: HC-05_Bluetooth_Module.TXD, R1.Pin_1, R2.Pin_0

custom parts:
  DIP - 4 pins: A DIP stand-in part for whatever IC you want. With 4 pins on a 300mil dual inline package (DIP) footprint.
